# Fritzing sketch circuit (saved by Fritzing 0.9.3b)
breadboards: 1

parts:
  RHT1 = Humidity and Temperature Sensor RHT03
  LCD1 = LCD screen
  R1 = Resistor [tolerance=±5% resistance=100k package=THT]
  R3 = Resistor [tolerance=±5% resistance=270 package=THT]
  Parça1 = Arduino Uno (Rev3)
  R4 = Resistor [tolerance=±5% resistance=10 package=THT]
  R5 = Rotary Potentiometer (Small) [maximum_resistance=10kΩ package=THT]

nets:
  VCC: RHT1.Vcc, LCD1.VDD, R3.Pin_0, Parça1.5V, R5.leg2
  N1: RHT1.Data-signal, Parça1.D6_PWM
  VSS: RHT1.GND_2, LCD1.VSS, LCD1.R/W, LCD1.LED-, Parça1.GND, R4.Pin_1, R5.leg1
  N2: LCD1.V0, R5.wiper
  N3: LCD1.RS, Parça1.D12/MISO
  N4: LCD1.E, Parça1.D11_PWM/MOSI
  N5: LCD1.DB4, Parça1.D5_PWM
  N6: LCD1.DB5, Parça1.D4
  N7: LCD1.DB6, Parça1.D3_PWM
  N8: LCD1.DB7, Parça1.D2
  N9: LCD1.LED+, R3.Pin_1
  N10: R1.Pin_0, Parça1.A0
  N11: R1.Pin_1, R4.Pin_0

notes:
  + uç
  -uç
